# Fritzing sketch Car (saved by Fritzing 0.9.3b)

parts:
  Часть1 = Arduino Nano (Rev3.0)
  драйвер_моторов_M1_и_M2 = L298 [package=multiwatt15]
  M1 = DC Motor
  M2 = DC Motor
  V1 = DC Power [voltage=5]
  радиомодуль = NRF24L01+ Breakout Board
  ультразвуковой_датчик = hc-sr04
  кнопка = Momentary Switch [package=ksa_sealed_tac_switch]
  R1_100_Ω = Resistor [tolerance=±5% resistance=220 package="2512 [SMD]"]

nets:
  GND: Часть1.GND, ультразвуковой_датчик.GND
  N1: Часть1.D6, радиомодуль.CE
  N2: Часть1.D7, радиомодуль.CS
  N3: Часть1.D8, ультразвуковой_датчик.Trig
  N4: Часть1.D9, ультразвуковой_датчик.Echo
  N5: Часть1.D11/MOSI, радиомодуль.MOSI
  N6: Часть1.D12/MISO, радиомодуль.MISO
  5V: Часть1.5V, ультразвуковой_датчик.VCC
  N7: Часть1.A5, R1_100_Ω.Pin_0
  N8: Часть1.A4, кнопка.1, кнопка.2
  N9: Часть1.A3, драйвер_моторов_M1_и_M2.IN4
  N10: Часть1.A2, драйвер_моторов_M1_и_M2.IN3
  N11: Часть1.A1, драйвер_моторов_M1_и_M2.IN2
  N12: Часть1.A0, драйвер_моторов_M1_и_M2.IN1
  3V3: Часть1.3V3, радиомодуль.VCC
  N13: Часть1.D13/SCK, радиомодуль.SCK
  N14: драйвер_моторов_M1_и_M2.OUT1, M2.pin_1
  N15: драйвер_моторов_M1_и_M2.OUT2, M2.pin_2
  N16: драйвер_моторов_M1_и_M2.VS, V1.V+
  GND_2: драйвер_моторов_M1_и_M2.GND, V1.V-, радиомодуль.GND, кнопка.3, кнопка.4, R1_100_Ω.Pin_1
  N17: драйвер_моторов_M1_и_M2.OUT3, M1.pin_1
  N18: драйвер_моторов_M1_и_M2.OUT4, M1.pin_2
